# Fritzing sketch arduino_sound (saved by Fritzing 0.9.3b)

parts:
  Arduino_Uno_R3 = Arduino Uno (Rev3)
  Passive_Buzzer = Buzzer 12mm [package=buzzer-12mm-ns]
  Toggle_Switch = Toggle Switch [package=THT]

nets:
  N1: Arduino_Uno_R3.D7, Passive_Buzzer.2
  N2: Arduino_Uno_R3.GND, Toggle_Switch.COM
  N3: Passive_Buzzer.1, Toggle_Switch.L2
